# Fritzing sketch led_strip_screen_rtc (saved by Fritzing 1.0.1rc)

parts:
  Part1 = Arduino Nano (Rev3.0)
  ZS-042_RTC1 = ZS-042 RTC Module
  RGB_SMD_LED1 = SMD RGB LED (WS2812) [package=5050]

nets:
  GND: Part1.GND, ZS-042_RTC1.GND, RGB_SMD_LED1.VSS
  N1: Part1.D2, RGB_SMD_LED1.DIn
  5V: Part1.5V, RGB_SMD_LED1.VCC
  N2: Part1.A5, ZS-042_RTC1.SCL
  N3: Part1.A4, ZS-042_RTC1.SDA
  3V3: Part1.3V3, ZS-042_RTC1.VCC
